// Logisim project alu.circ as structural Verilog: 4 circuits, main circuit main
module main (
  input  [31:0] X,
  input  [31:0] Y,
  input  [3:0] Switch,
  output Signed_Overflow,
  output Equal,
  output [31:0] Result
);

  wire addOverflow, comparator_1_lt, comparator_2_lt, subOverflow;
  wire [31:0] add, addu, \and , \or , sll, slt, sltu, sra, srl, sub, subu, \xor ;

  _32bit_add_sub u_32bit_add_sub_1 (
    .in_2(X), .in_3(Y), .in_1(1'b0), .overflow(addOverflow), .out(add));  // open: carryOut
  _32bit_add_sub u_32bit_add_sub_2 (
    .in_2(X), .in_3(Y), .in_1(1'b1), .overflow(subOverflow), .out(sub));  // open: carryOut
  Shifter #(.width(32)) shifter_1 (.in(Y), .\dist (X[4:0]), .out(sll));
  Shifter #(.width(32), .shift("lr")) shifter_2 (.in(Y), .\dist (X[4:0]), .out(srl));
  Shifter #(.width(32), .shift("ar")) shifter_3 (.in(Y), .\dist (X[4:0]), .out(sra));
  Adder #(.width(32)) adder_1 (.a(X), .b(Y), .out(addu));  // open: cin, cout
  Subtractor #(.width(32)) subtractor_1 (.a(X), .b(Y), .out(subu));  // open: bin, bout
  assign \and  = X & Y;  // AND_Gate and_1, 32 bits wide
  assign \or  = X | Y;  // OR_Gate or_1, 32 bits wide
  assign \xor  = X ^ Y;  // XOR_Gate xor_1, 32 bits wide
  Comparator #(.width(32)) comparator_1 (.a(X), .b(Y), .lt(comparator_1_lt));  // open: gt, eq
  Comparator #(.width(32), .mode("unsigned")) comparator_2 (.a(X), .b(Y), .lt(comparator_2_lt));  // open: gt, eq
  assign slt = {{31{1'b0}}, comparator_1_lt};  // Bit_Extender bit_extender_1
  assign sltu = {{31{1'b0}}, comparator_2_lt};  // Bit_Extender bit_extender_2
  Multiplexer #(.select(4), .width(32)) multiplexer_1 (
    .in0(sll), .in1(srl), .in2(sra), .in3(add), .in4(addu), .in5(sub), .in6(subu), .in7(\and ), .in8(\or ),
    .in9(\xor ), .in10(slt), .in11(sltu), .out(Result), .sel(Switch));  // open: in12, in13, in14, in15, en
  Comparator #(.width(32)) comparator_3 (.a(X), .b(Y), .eq(Equal));  // open: gt, lt
  Multiplexer #(.select(4)) multiplexer_2 (
    .in0(1'b0), .in1(1'b0), .in2(1'b0), .in3(addOverflow), .in4(1'b0), .in5(subOverflow), .in6(1'b0),
    .in7(1'b0), .in8(1'b0), .in9(1'b0), .in10(1'b0), .in11(1'b0), .out(Signed_Overflow), .sel(Switch));  // open: in12, in13, in14, in15, en

  // Other names for the same wires on the sheet: overflow = Signed_Overflow; S[3:0] = Switch

  // Notes on the sheet:
  //   INPUTS to your circuit
  //   sll
  //   srl
  //   sra
  //   DON'T CHANGE THE LOCATIONS OF THE INPUTS AND OUTPUTS!
  //   OUTPUTS from your circuit
endmodule

module _4bit_add_sub (
  input  in_1,
  input  [3:0] in_2,
  input  [3:0] in_3,
  output [3:0] out,
  output out_2,
  output out_3
);

  wire adder_1_cout, adder_2_cout, adder_3_cout;

  Adder #(.width(1)) adder_1 (.a(in_2[0]), .b(in_3[0]), .out(out[0]), .cin(in_1), .cout(adder_1_cout));
  Adder #(.width(1)) adder_2 (.a(in_2[1]), .b(in_3[1]), .out(out[1]), .cin(adder_1_cout), .cout(adder_2_cout));
  Adder #(.width(1)) adder_3 (.a(in_2[2]), .b(in_3[2]), .out(out[2]), .cin(adder_2_cout), .cout(adder_3_cout));
  Adder #(.width(1)) adder_4 (.a(in_2[3]), .b(in_3[3]), .out(out[3]), .cin(adder_3_cout), .cout(out_3));
  xor xor_1 (out_2, adder_3_cout, out_3);
endmodule

module _16bit_add_sub (
  input  in_1,
  input  [15:0] in_2,
  input  [15:0] in_3,
  output [15:0] out,
  output overflow,
  output out_2
);

  wire n4bit_add_sub_1_out_3, n4bit_add_sub_2_out_3, n4bit_add_sub_3_out_3;

  _4bit_add_sub u_4bit_add_sub_1 (
    .in_2(in_2[3:0]), .in_3(in_3[3:0]), .in_1(in_1), .out_3(n4bit_add_sub_1_out_3), .out(out[3:0]));  // open: out_2
  _4bit_add_sub u_4bit_add_sub_2 (
    .in_2(in_2[7:4]), .in_3(in_3[7:4]), .in_1(n4bit_add_sub_1_out_3), .out_3(n4bit_add_sub_2_out_3),
    .out(out[7:4]));  // open: out_2
  _4bit_add_sub u_4bit_add_sub_3 (
    .in_2(in_2[11:8]), .in_3(in_3[11:8]), .in_1(n4bit_add_sub_2_out_3), .out_3(n4bit_add_sub_3_out_3),
    .out(out[11:8]));  // open: out_2
  _4bit_add_sub u_4bit_add_sub_4 (
    .in_2(in_2[15:12]), .in_3(in_3[15:12]), .in_1(n4bit_add_sub_3_out_3), .out_3(out_2), .out_2(overflow),
    .out(out[15:12]));
endmodule

module _32bit_add_sub (
  input  in_1,
  input  [31:0] in_2,
  input  [31:0] in_3,
  output [31:0] out,
  output overflow,
  output carryOut
);

  wire n16bit_add_sub_1_out_2;
  wire [15:0] bit_extender_1_out, xor_1_out, xor_2_out;

  assign bit_extender_1_out = {{15{in_1}}, in_1};  // Bit_Extender bit_extender_1
  _16bit_add_sub u_16bit_add_sub_1 (
    .in_2(xor_1_out), .in_3(in_2[15:0]), .in_1(in_1), .out_2(n16bit_add_sub_1_out_2), .out(out[15:0]));  // open: overflow
  _16bit_add_sub u_16bit_add_sub_2 (
    .in_2(xor_2_out), .in_3(in_2[31:16]), .in_1(n16bit_add_sub_1_out_2), .out_2(carryOut),
    .overflow(overflow), .out(out[31:16]));
  assign xor_1_out = in_3[15:0] ^ bit_extender_1_out;  // XOR_Gate xor_1, 16 bits wide
  assign xor_2_out = in_3[31:16] ^ bit_extender_1_out;  // XOR_Gate xor_2, 16 bits wide
endmodule
